# Fritzing sketch 001_UltraSonic (saved by Fritzing 0.9.4)
breadboards: 1

parts:
  U2 = ESP32-38PinWide [part_number=ESP32-38PinWide]
  HC-SR04_Sensor_1 = HC-SR04 Ultrasonic Distance Sensor

nets:
  GND: U2.GND, HC-SR04_Sensor_1.GND
  VIN: U2.VIN, HC-SR04_Sensor_1.VCC
  N1: U2.GPIO2, HC-SR04_Sensor_1.TRIG
  N2: U2.GPIO5, HC-SR04_Sensor_1.ECHO

custom parts:
  ESP32-38PinWide: Generic 38-Pin ESP32 with wide format (only access to one side of pins on a breadboard) based on Stephen Lilley's HiLetgo ESP-WROOM-32 ESP32 ESP-32S Development Board.
