# Fritzing sketch 002_Blink3LEDs (saved by Fritzing 0.9.4)
breadboards: 1

parts:
  U2 = ESP32-38PinWide [part_number=ESP32-38PinWide]
  R4 = Resistor [tolerance=±5% resistance=330 package=THT]
  LED4 = LED - 5mm [color="Red (633nm)" package="5 mm [THT]"]
  R5 = Resistor [tolerance=±5% resistance=330 package=THT]
  LED5 = LED - 5mm [color="Yellow (574nm)" package="5 mm [THT]"]
  R6 = Resistor [tolerance=±5% resistance=330 package=THT]
  LED6 = LED - 5mm [color="Green (555nm)" package="5 mm [THT]"]

nets:
  N1: U2.GPIO27, R6.Pin_1
  N2: U2.GPIO14, R5.Pin_1
  N3: U2.GPIO12, R4.Pin_1
  N4: U2.GND, LED4.cathode, LED5.cathode, LED6.cathode
  N5: R4.Pin_0, LED4.anode
  N6: R5.Pin_0, LED5.anode
  N7: R6.Pin_0, LED6.anode

custom parts:
  ESP32-38PinWide: Generic 38-Pin ESP32 with wide format (only access to one side of pins on a breadboard) based on Stephen Lilley's HiLetgo ESP-WROOM-32 ESP32 ESP-32S Development Board.

// code stored in the sketch: 02_3LED_Blink.ino

/*
  Blinking LEDs

  Turns each LED of 3 for one second, then off for one second, repeatedly.

   The circuit:
  - RED LED attached from digital pin 5 to ground.
  - GREEN LED attached from digital pin 6 to ground.
  - BLUE LED attached from digital pin 7 to ground.

  by Ganesh Butcha
*/


int led1=5;               // assign digital pin 5 to a variable
int led2=6;
int led3=7;
int waitTime=1000;        // wait time is 1 second

void setup() {
  // put your setup code here, to run once:
  pinMode(led1, OUTPUT);    // initialize digital pin as an output
  pinMode(led2, OUTPUT);    
  pinMode(led3, OUTPUT);

}

void loop() {
  // put your main code here, to run repeatedly:
  digitalWrite(led1, HIGH);   // turn the LED on (HIGH is the voltage level)
  digitalWrite(led2, LOW);    // turn the LED off (LOW is the voltage level)
  digitalWrite(led3, LOW);
  delay(waitTime);                 // wait for a second
  
  digitalWrite(led1, LOW);
  digitalWrite(led2, HIGH);
  digitalWrite(led3, LOW);
  delay(waitTime);

  digitalWrite(led1, LOW);
  digitalWrite(led2, LOW);
  digitalWrite(led3, HIGH);
  delay(waitTime);
  
}
