# Fritzing sketch car (saved by Fritzing 0.9.4)
breadboards: 2

parts:
  U1 = ESP32-38PinWide [part_number=ESP32-38PinWide]
  BAT2 = BC9VPC [package=bc9vpc]
  R1 = Resistor [tolerance=±5% resistance=330 package="2512 [SMD]"]
  LED1 = smd LED [color="White (4500K)" package="0805 [SMD]"]
  L298N1 = L298N DC motor driver
  M4 = DC Motor
  M5 = DC Motor
  M6 = DC Motor
  M7 = DC Motor

nets:
  N1: U1.GPIO12, R1.Pin_0
  GND: U1.GND, BAT2.V-, LED1.cathode, L298N1.GND
  VIN: U1.VIN, BAT2.V+, L298N1.5V
  N2: R1.Pin_1, LED1.anode
  N3: L298N1.OUT1, M5.pin_2, M6.pin_2
  N4: L298N1.OUT2, M5.pin_1, M6.pin_1
  N5: L298N1.OUT3, M4.pin_2, M7.pin_2
  N6: L298N1.OUT4, M7.pin_1

custom parts:
  ESP32-38PinWide: Generic 38-Pin ESP32 with wide format (only access to one side of pins on a breadboard) based on Stephen Lilley's HiLetgo ESP-WROOM-32 ESP32 ESP-32S Development Board.
  L298N DC motor driver: 2x DC motor driver with 78M05 positive voltage regulator (7..35 V) L298N: max 46 V, 2 A Set 5 V Enable jumper to enable 5 V regultor (needed for the L298N) and +5 V output at screw terminal or supply external +5 V at screw terminal Set ENA and/or ENB to +5 V to enable motor permanently or supply ENA and/or ENB with PWM signal IN1 and IN2 set rotation directory for motor A (OUT1/OUT2) IN2 and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
